# Fritzing sketch cartaodeponto (saved by Fritzing 0.9.4)
breadboards: 1

parts:
  Raspberry_Pi1 = Raspberry Pi B rev2
  PCB2 = RTC_DS1302_module
  Bauteil1 = RFID-RC522-v2
  S1 = Pushbutton [package="[THT]"]
  S2 = Pushbutton [package="[THT]"]
  LED1 = RGB LED (com. cathode, rgb) [package="5 mm [THT]"]
  Display1 = LCD screen 16x2 IIC [part_number=101290]

nets:
  3V3: Raspberry_Pi1.3V3, PCB2.VCC, Bauteil1.3.3V
  5V: Raspberry_Pi1.5V, Display1.VCC
  N1: Raspberry_Pi1.GPIO_2, PCB2.RST
  GND: Raspberry_Pi1.GND, PCB2.GND, Bauteil1.GND, LED1.common_cathode, Display1.GND
  N2: S1.Pin_1, S1.Pin_2
  N3: S1.Pin_3, S1.Pin_4
  N4: S2.Pin_1, S2.Pin_2
  N5: S2.Pin_3, S2.Pin_4

custom parts:
  RTC_DS1302_module: Arduino module DS1302 SPI Real Time Clock
  RFID-RC522-v2: A simple China made RFID-RC522 Reader; do check the pin labels, as this is a MFRC522 based clone.
  LCD screen 16x2 IIC: LCD screen with HD44780 controller enables showing text, symbols, value or anything else that comes from Croduino/Arduino. It is capable of showing 16 symbols in two lines and therefore can be used in many projects that need to send clearly visible and legible output information.. • Color of symbols: White • Backlight: Blue • Dimensions: 80 x 36 x 12 mm • Screen dimensions: 64.5 x 16 mm •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
